// Logisim project control_logic.circ as structural Verilog: 1 circuit, main circuit control_logic
module control_logic (
  input  [31:0] inst,
  input  BrEq,
  input  BrLt,
  output PCSel,
  output RegWEn,
  output [2:0] ImmSel,
  output BrUn,
  output ASel,
  output BSel,
  output [3:0] ALUSel,
  output MemRW,
  output [1:0] WBSel,
  output CSRSel,
  output CSRWen,
  output [1:0] StoreSel
);

  wire and_2_out, and_3_out, and_4_out, and_5_out, and_6_out, and_7_out, and_8_out, and_9_out, and_10_out,
       and_11_out, and_12_out, and_13_out, and_14_out, and_15_out, and_16_out, and_17_out, and_18_out,
       and_19_out, and_20_out, and_21_out, and_22_out, and_23_out, and_24_out, and_25_out, beq_out, bge_out,
       bgeu_out, blt_out, bltu_out, bne_out, comparator_2_eq, comparator_3_eq, comparator_4_eq,
       comparator_5_eq, comparator_6_eq, comparator_7_eq, comparator_8_eq, comparator_9_eq, comparator_10_eq,
       comparator_11_eq, comparator_12_eq, comparator_13_eq, comparator_14_eq, comparator_15_eq,
       comparator_16_eq, comparator_17_eq, comparator_18_eq, comparator_19_eq, comparator_20_eq,
       comparator_21_eq, comparator_22_eq, comparator_23_eq, comparator_24_eq, comparator_25_eq,
       comparator_26_eq, comparator_27_eq, comparator_28_eq, comparator_29_eq, comparator_30_eq,
       comparator_31_eq, comparator_32_eq, comparator_33_eq, comparator_34_eq, comparator_35_eq,
       comparator_36_eq, comparator_37_eq, comparator_38_eq, comparator_39_eq, comparator_40_eq,
       comparator_41_eq, comparator_42_eq, comparator_43_eq, comparator_44_eq, comparator_45_eq,
       comparator_46_eq, comparator_47_eq, comparator_48_eq, comparator_49_eq, comparator_50_eq,
       comparator_51_eq, comparator_52_eq, comparator_53_eq, comparator_54_eq, comparator_56_eq,
       comparator_57_eq, comparator_58_eq, comparator_59_eq, lb_out, lh_out, lw_out, or_1_out, or_2_out,
       or_3_out, or_4_out, or_5_out, or_6_out, or_7_out, or_8_out, or_9_out, or_10_out, or_11_out, or_12_out,
       or_13_out, or_15_out, or_16_out, or_17_out, or_18_out;

  Comparator #(.mode("unsigned"), .width(7)) comparator_1 (.a(inst[6:0]), .b(7'b1110011), .eq(CSRWen));  // open: gt, lt
  Comparator #(.mode("unsigned"), .width(3)) comparator_2 (
    .a(inst[14:12]), .b(3'b001), .eq(comparator_2_eq));  // open: gt, lt
  and and_1 (CSRSel, CSRWen, comparator_2_eq);
  Comparator #(.mode("unsigned"), .width(7)) comparator_3 (
    .a(inst[6:0]), .b(7'b0000011), .eq(comparator_3_eq));  // open: gt, lt
  Comparator #(.mode("unsigned"), .width(7)) comparator_4 (
    .a(inst[6:0]), .b(7'b0010011), .eq(comparator_4_eq));  // open: gt, lt
  Comparator #(.mode("unsigned"), .width(7)) comparator_5 (
    .a(inst[6:0]), .b(7'b1100111), .eq(comparator_5_eq));  // open: gt, lt
  Comparator #(.mode("unsigned"), .width(7)) comparator_6 (
    .a(inst[6:0]), .b(7'b0100011), .eq(comparator_6_eq));  // open: gt, lt
  Comparator #(.mode("unsigned"), .width(7)) comparator_7 (
    .a(inst[6:0]), .b(7'b1100011), .eq(comparator_7_eq));  // open: gt, lt
  Comparator #(.mode("unsigned"), .width(7)) comparator_8 (
    .a(inst[6:0]), .b(7'b0010111), .eq(comparator_8_eq));  // open: gt, lt
  Comparator #(.mode("unsigned"), .width(7)) comparator_9 (
    .a(inst[6:0]), .b(7'b0110111), .eq(comparator_9_eq));  // open: gt, lt
  Comparator #(.mode("unsigned"), .width(7)) comparator_10 (
    .a(inst[6:0]), .b(7'b1101111), .eq(comparator_10_eq));  // open: gt, lt
  Comparator #(.mode("unsigned"), .width(7)) comparator_11 (
    .a(inst[6:0]), .b(7'b1110011), .eq(comparator_11_eq));  // open: gt, lt
  Comparator #(.mode("unsigned"), .width(7)) comparator_12 (
    .a(inst[6:0]), .b(7'b0110011), .eq(comparator_12_eq));  // open: gt, lt
  Comparator #(.mode("unsigned"), .width(3)) comparator_13 (
    .a(inst[14:12]), .b(3'b000), .eq(comparator_13_eq));  // open: gt, lt
  Comparator #(.mode("unsigned"), .width(7)) comparator_14 (
    .a(inst[31:25]), .b({7{1'b0}}), .eq(comparator_14_eq));  // open: gt, lt
  Comparator #(.mode("unsigned"), .width(7)) comparator_15 (
    .a(inst[31:25]), .b(7'b0000001), .eq(comparator_15_eq));  // open: gt, lt
  Comparator #(.mode("unsigned"), .width(7)) comparator_16 (
    .a(inst[31:25]), .b(7'b0100000), .eq(comparator_16_eq));  // open: gt, lt
  Comparator #(.mode("unsigned"), .width(3)) comparator_17 (
    .a(inst[14:12]), .b(3'b111), .eq(comparator_17_eq));  // open: gt, lt
  Comparator #(.mode("unsigned"), .width(3)) comparator_18 (
    .a(inst[14:12]), .b(3'b110), .eq(comparator_18_eq));  // open: gt, lt
  Comparator #(.mode("unsigned"), .width(3)) comparator_19 (
    .a(inst[14:12]), .b(3'b100), .eq(comparator_19_eq));  // open: gt, lt
  Comparator #(.mode("unsigned"), .width(3)) comparator_20 (
    .a(inst[14:12]), .b(3'b101), .eq(comparator_20_eq));  // open: gt, lt
  Comparator #(.mode("unsigned"), .width(3)) comparator_21 (
    .a(inst[14:12]), .b(3'b001), .eq(comparator_21_eq));  // open: gt, lt
  Comparator #(.mode("unsigned"), .width(3)) comparator_22 (
    .a(inst[14:12]), .b(3'b010), .eq(comparator_22_eq));  // open: gt, lt
  Comparator #(.mode("unsigned"), .width(3)) comparator_23 (
    .a(inst[14:12]), .b(3'b011), .eq(comparator_23_eq));  // open: gt, lt
  Comparator #(.mode("unsigned"), .width(7)) comparator_24 (
    .a(inst[6:0]), .b(7'b0110111), .eq(comparator_24_eq));  // open: gt, lt
  Comparator #(.mode("unsigned"), .width(7)) comparator_25 (
    .a(inst[6:0]), .b(7'b0000011), .eq(comparator_25_eq));  // open: gt, lt
  Comparator #(.mode("unsigned"), .width(7)) comparator_26 (
    .a(inst[6:0]), .b(7'b0010011), .eq(comparator_26_eq));  // open: gt, lt
  Comparator #(.mode("unsigned"), .width(7)) comparator_27 (
    .a(inst[6:0]), .b(7'b0100011), .eq(comparator_27_eq));  // open: gt, lt
  Comparator #(.mode("unsigned"), .width(7)) comparator_28 (
    .a(inst[6:0]), .b(7'b1100011), .eq(comparator_28_eq));  // open: gt, lt
  Comparator #(.mode("unsigned"), .width(7)) comparator_29 (
    .a(inst[6:0]), .b(7'b0010111), .eq(comparator_29_eq));  // open: gt, lt
  Comparator #(.mode("unsigned"), .width(7)) comparator_30 (
    .a(inst[6:0]), .b(7'b1101111), .eq(comparator_30_eq));  // open: gt, lt
  Comparator #(.mode("unsigned"), .width(7)) comparator_31 (
    .a(inst[6:0]), .b(7'b1100111), .eq(comparator_31_eq));  // open: gt, lt
  or or_1 (or_1_out, comparator_3_eq, comparator_4_eq, comparator_5_eq);
  or or_2 (or_2_out, comparator_8_eq, comparator_9_eq);
  and and_2 (and_2_out, comparator_12_eq, comparator_13_eq, comparator_14_eq);
  and and_3 (and_3_out, comparator_26_eq, comparator_13_eq);
  assign ImmSel = or_1_out ? 3'b000 : 3'bz;  // Controlled_Buffer controlled_buffer_1
  assign ImmSel = comparator_6_eq ? 3'b001 : 3'bz;  // Controlled_Buffer controlled_buffer_2
  assign ImmSel = comparator_7_eq ? 3'b010 : 3'bz;  // Controlled_Buffer controlled_buffer_3
  assign ImmSel = or_2_out ? 3'b011 : 3'bz;  // Controlled_Buffer controlled_buffer_4
  assign ImmSel = comparator_10_eq ? 3'b100 : 3'bz;  // Controlled_Buffer controlled_buffer_5
  assign ImmSel = comparator_11_eq ? 3'b101 : 3'bz;  // Controlled_Buffer controlled_buffer_6
  and and_4 (and_4_out, comparator_12_eq, comparator_17_eq);
  and and_5 (and_5_out, comparator_17_eq, comparator_26_eq);
  and and_6 (and_6_out, comparator_18_eq, comparator_12_eq);
  and and_7 (and_7_out, comparator_18_eq, comparator_26_eq);
  and and_8 (and_8_out, comparator_12_eq, comparator_19_eq);
  and and_9 (and_9_out, comparator_19_eq, comparator_26_eq);
  and and_10 (and_10_out, comparator_12_eq, comparator_20_eq, comparator_14_eq);
  and and_11 (and_11_out, comparator_20_eq, comparator_14_eq, comparator_26_eq);
  and and_12 (and_12_out, comparator_12_eq, comparator_20_eq, comparator_16_eq);
  and and_13 (and_13_out, comparator_20_eq, comparator_16_eq, comparator_26_eq);
  and and_14 (and_14_out, comparator_12_eq, comparator_21_eq, comparator_14_eq);
  and and_15 (and_15_out, comparator_14_eq, comparator_21_eq, comparator_26_eq);
  and and_16 (and_16_out, comparator_12_eq, comparator_22_eq, comparator_14_eq);
  and and_17 (and_17_out, comparator_22_eq, comparator_26_eq);
  and and_18 (and_18_out, comparator_12_eq, comparator_13_eq, comparator_15_eq);
  and and_19 (and_19_out, comparator_12_eq, comparator_23_eq, comparator_15_eq);
  and and_20 (and_20_out, comparator_12_eq, comparator_13_eq, comparator_16_eq);
  and and_21 (and_21_out, comparator_12_eq, comparator_21_eq, comparator_15_eq);
  or or_3 (or_3_out, and_4_out, and_5_out);
  or or_4 (or_4_out, and_6_out, and_7_out);
  or or_5 (or_5_out, and_8_out, and_9_out);
  or or_6 (or_6_out, and_10_out, and_11_out);
  or or_7 (or_7_out, and_12_out, and_13_out);
  or or_8 (or_8_out, and_14_out, and_15_out);
  or or_9 (or_9_out, and_16_out, and_17_out);
  or or_10 (or_10_out, and_2_out, and_3_out, comparator_25_eq, comparator_27_eq, comparator_28_eq, comparator_29_eq, comparator_30_eq, comparator_31_eq);
  assign ALUSel = or_10_out ? 4'b0000 : 4'bz;  // Controlled_Buffer controlled_buffer_7
  assign ALUSel = or_3_out ? 4'b0001 : 4'bz;  // Controlled_Buffer controlled_buffer_8
  assign ALUSel = or_4_out ? 4'b0010 : 4'bz;  // Controlled_Buffer controlled_buffer_9
  assign ALUSel = or_5_out ? 4'b0011 : 4'bz;  // Controlled_Buffer controlled_buffer_10
  assign ALUSel = or_6_out ? 4'b0100 : 4'bz;  // Controlled_Buffer controlled_buffer_11
  assign ALUSel = or_7_out ? 4'b0101 : 4'bz;  // Controlled_Buffer controlled_buffer_12
  assign ALUSel = or_8_out ? 4'b0110 : 4'bz;  // Controlled_Buffer controlled_buffer_13
  assign ALUSel = or_9_out ? 4'b0111 : 4'bz;  // Controlled_Buffer controlled_buffer_14
  assign ALUSel = and_18_out ? 4'b1010 : 4'bz;  // Controlled_Buffer controlled_buffer_15
  assign ALUSel = and_19_out ? 4'b1011 : 4'bz;  // Controlled_Buffer controlled_buffer_16
  assign ALUSel = and_20_out ? 4'b1100 : 4'bz;  // Controlled_Buffer controlled_buffer_17
  assign ALUSel = comparator_24_eq ? 4'b1101 : 4'bz;  // Controlled_Buffer controlled_buffer_18
  assign ALUSel = and_21_out ? 4'b1110 : 4'bz;  // Controlled_Buffer controlled_buffer_19
  Comparator #(.mode("unsigned"), .width(7)) comparator_32 (
    .a(inst[6:0]), .b(7'b1100011), .eq(comparator_32_eq));  // open: gt, lt
  Comparator #(.mode("unsigned"), .width(3)) comparator_33 (
    .a(inst[14:12]), .b(3'b000), .eq(comparator_33_eq));  // open: gt, lt
  Comparator #(.mode("unsigned"), .width(3)) comparator_34 (
    .a(inst[14:12]), .b(3'b001), .eq(comparator_34_eq));  // open: gt, lt
  Comparator #(.mode("unsigned"), .width(3)) comparator_35 (
    .a(inst[14:12]), .b(3'b100), .eq(comparator_35_eq));  // open: gt, lt
  Comparator #(.mode("unsigned"), .width(3)) comparator_36 (
    .a(inst[14:12]), .b(3'b101), .eq(comparator_36_eq));  // open: gt, lt
  Comparator #(.mode("unsigned"), .width(3)) comparator_37 (
    .a(inst[14:12]), .b(3'b110), .eq(comparator_37_eq));  // open: gt, lt
  Comparator #(.mode("unsigned"), .width(3)) comparator_38 (
    .a(inst[14:12]), .b(3'b111), .eq(comparator_38_eq));  // open: gt, lt
  Comparator #(.mode("unsigned"), .width(7)) comparator_39 (
    .a(inst[6:0]), .b(7'b1101111), .eq(comparator_39_eq));  // open: gt, lt
  Comparator #(.mode("unsigned"), .width(7)) comparator_40 (
    .a(inst[6:0]), .b(7'b1100111), .eq(comparator_40_eq));  // open: gt, lt
  and beq (beq_out, comparator_32_eq, comparator_33_eq);
  and bne (bne_out, comparator_32_eq, comparator_34_eq);
  and blt (blt_out, comparator_32_eq, comparator_35_eq);
  and bge (bge_out, comparator_32_eq, comparator_36_eq);
  and bltu (bltu_out, comparator_32_eq, comparator_37_eq);
  and bgeu (bgeu_out, comparator_32_eq, comparator_38_eq);
  or or_11 (or_11_out, comparator_39_eq, comparator_40_eq);
  or or_12 (or_12_out, blt_out, bltu_out);
  or or_13 (or_13_out, bge_out, bgeu_out);
  or or_14 (BrUn, bltu_out, bgeu_out);
  Comparator #(.mode("unsigned"), .width(7)) comparator_41 (
    .a(inst[6:0]), .b(7'b1100011), .eq(comparator_41_eq));  // open: gt, lt
  Comparator #(.mode("unsigned"), .width(7)) comparator_42 (
    .a(inst[6:0]), .b(7'b0010111), .eq(comparator_42_eq));  // open: gt, lt
  Comparator #(.mode("unsigned"), .width(7)) comparator_43 (
    .a(inst[6:0]), .b(7'b1101111), .eq(comparator_43_eq));  // open: gt, lt
  Comparator #(.mode("unsigned"), .width(7)) comparator_44 (
    .a(inst[6:0]), .b(7'b0110011), .eq(comparator_44_eq));  // open: gt, lt
  and and_22 (and_22_out, BrEq, beq_out);
  and and_23 (and_23_out, ~BrEq, bne_out);  // AND_Gate
  and and_24 (and_24_out, BrLt, or_12_out);
  and and_25 (and_25_out, ~BrLt, or_13_out);  // AND_Gate
  Comparator #(.mode("unsigned"), .width(7)) comparator_45 (
    .a(inst[6:0]), .b(7'b0100011), .eq(comparator_45_eq));  // open: gt, lt
  Comparator #(.mode("unsigned"), .width(7)) comparator_46 (
    .a(inst[6:0]), .b(7'b1100011), .eq(comparator_46_eq));  // open: gt, lt
  Comparator #(.mode("unsigned"), .width(7)) comparator_47 (
    .a(inst[6:0]), .b(7'b1110011), .eq(comparator_47_eq));  // open: gt, lt
  Comparator #(.mode("unsigned"), .width(7)) comparator_48 (
    .a(inst[6:0]), .b(7'b1101111), .eq(comparator_48_eq));  // open: gt, lt
  Comparator #(.mode("unsigned"), .width(7)) comparator_49 (
    .a(inst[6:0]), .b(7'b1100111), .eq(comparator_49_eq));  // open: gt, lt
  Comparator #(.mode("unsigned"), .width(7)) comparator_50 (
    .a(inst[6:0]), .b(7'b0010111), .eq(comparator_50_eq));  // open: gt, lt
  Comparator #(.mode("unsigned"), .width(7)) comparator_51 (
    .a(inst[6:0]), .b(7'b0110111), .eq(comparator_51_eq));  // open: gt, lt
  Comparator #(.mode("unsigned"), .width(7)) comparator_52 (
    .a(inst[6:0]), .b(7'b0010011), .eq(comparator_52_eq));  // open: gt, lt
  Comparator #(.mode("unsigned"), .width(7)) comparator_53 (
    .a(inst[6:0]), .b(7'b0110011), .eq(comparator_53_eq));  // open: gt, lt
  Comparator #(.mode("unsigned"), .width(7)) comparator_54 (
    .a(inst[6:0]), .b(7'b0000011), .eq(comparator_54_eq));  // open: gt, lt
  Comparator #(.mode("unsigned"), .width(7)) comparator_55 (.a(inst[6:0]), .b(7'b0100011), .eq(MemRW));  // open: gt, lt
  Comparator #(.mode("unsigned"), .width(7)) comparator_56 (
    .a(inst[6:0]), .b(7'b0000011), .eq(comparator_56_eq));  // open: gt, lt
  Comparator #(.mode("unsigned"), .width(3)) comparator_57 (
    .a(inst[14:12]), .b(3'b000), .eq(comparator_57_eq));  // open: gt, lt
  Comparator #(.mode("unsigned"), .width(3)) comparator_58 (
    .a(inst[14:12]), .b(3'b001), .eq(comparator_58_eq));  // open: gt, lt
  Comparator #(.mode("unsigned"), .width(3)) comparator_59 (
    .a(inst[14:12]), .b(3'b010), .eq(comparator_59_eq));  // open: gt, lt
  or or_15 (or_15_out, comparator_41_eq, comparator_42_eq, comparator_43_eq);
  or or_16 (or_16_out, comparator_45_eq, comparator_46_eq, comparator_47_eq);
  or or_17 (or_17_out, comparator_48_eq, comparator_49_eq);
  or or_18 (or_18_out, comparator_50_eq, comparator_51_eq, comparator_52_eq, comparator_53_eq);
  and lb (lb_out, comparator_56_eq, comparator_57_eq);
  and lh (lh_out, comparator_56_eq, comparator_58_eq);
  and lw (lw_out, comparator_56_eq, comparator_59_eq);
  or or_19 (PCSel, and_22_out, and_23_out, or_11_out, and_24_out, and_25_out);
  not not_1 (ASel, or_15_out);
  not not_2 (BSel, comparator_44_eq);
  not not_3 (RegWEn, or_16_out);
  assign WBSel = or_17_out ? 2'b00 : 2'bz;  // Controlled_Buffer controlled_buffer_20
  assign WBSel = or_18_out ? 2'b01 : 2'bz;  // Controlled_Buffer controlled_buffer_21
  assign WBSel = comparator_54_eq ? 2'b10 : 2'bz;  // Controlled_Buffer controlled_buffer_22
  assign StoreSel = lb_out ? 2'b00 : 2'bz;  // Controlled_Buffer controlled_buffer_23
  assign StoreSel = lh_out ? 2'b01 : 2'bz;  // Controlled_Buffer controlled_buffer_24
  assign StoreSel = lw_out ? 2'b10 : 2'bz;  // Controlled_Buffer controlled_buffer_25

  // Other names for the same wires on the sheet: funct3[2:0] = inst[14:12]; funct7[6:0] = inst[31:25];
  //   Opcode[6:0] = inst[6:0]

  // Notes on the sheet:
  //   INPUTS to your circuit
  //   What is the instruction?
  //   CSR
  //   DON'T CHANGE THE LOCATIONS OF THE INPUTS AND OUTPUTS!
  //   OUTPUT from your circuit
  //   Where is the immediate?
  //   I
  //   S
  //   SB
  //   U
  //   UJ
  //   CSR
  //   What does ALU do?
  //   AND
  //   OR
  //   XOR
  //   SRL
  //   SRA
  //   SLL
  //   SLT
  //   MUL
  //   MULHU
  //   SUB
  //   BSEL
  //   MULH
  //   ADD
  //   What does PC become?
  //   What does ALU get?
  //   When to write back to rd?
  //   What to write back to rd?
  //   When to write to memory?
  //   How much to write to memory?
endmodule
