// Logisim project cpu.circ as structural Verilog: 1 circuit, main circuit cpu
module cpu (
  input  clk,
  input  [31:0] INSTRUCTION,
  input  [31:0] READ_DATA,
  output [31:0] WRITE_ADDRESS,
  output [31:0] PROGRAM_COUNTER,
  output [31:0] ra,
  output [31:0] sp,
  output [31:0] t0,
  output [31:0] t1,
  output [31:0] t2,
  output [31:0] s0,
  output [31:0] s1,
  output [31:0] a0,
  output [31:0] tohost,
  output [3:0] WRITE_ENABLE,
  output [31:0] WRITE_DATA
);

  wire ASel, BrEq, BrLt, BrUn, BSel, CSRSel, CSRWEn, MemRW, PCSel, RegWEn;
  wire [1:0] LoadSel, StoreSel, WBSel;
  wire [2:0] ImmSel;
  wire [3:0] ALUSel, multiplexer_8_out, multiplexer_9_out, multiplexer_10_out;
  wire [4:0] register_1_q_2, register_1_q_3;
  wire [7:0] multiplexer_12_out;
  wire [11:0] CSR_address;
  wire [14:0] register_1_q;
  wire [15:0] multiplexer_13_out;
  wire [31:0] adder_1_out, bit_extender_1_out, bit_extender_2_out, imm, multiplexer_1_out, multiplexer_2_out,
       multiplexer_3_out, multiplexer_4_out, multiplexer_5_out, PC_n_4, PC_stored, READ_DATA_FINAL, rs1, rs2,
       WBData;

  Adder #(.width(32)) adder_1 (.a(PROGRAM_COUNTER), .b(32'h4), .out(adder_1_out));  // open: cin, cout
  Multiplexer #(.enable("false"), .width(32)) multiplexer_1 (
    .in0(adder_1_out), .in1(WRITE_ADDRESS), .out(multiplexer_1_out), .sel(PCSel));
  Multiplexer #(.enable("false"), .width(32)) multiplexer_2 (
    .in0(INSTRUCTION), .in1(32'h13), .out(multiplexer_2_out), .sel(PCSel));
  Register #(.width(32)) PC (.D(multiplexer_1_out), .en(1'b1), .clk(clk), .Q(PROGRAM_COUNTER));  // open: clr
  Register #(.width(32)) register_1 (
    .D(multiplexer_2_out), .en(1'b1), .clk(clk),
    .Q({CSR_address, register_1_q_2, register_1_q[14:12], register_1_q_3, register_1_q[6:0]}));  // open: clr
  Register #(.width(32)) register_2 (.D(adder_1_out), .en(1'b1), .clk(clk), .Q(PC_n_4));  // open: clr
  Register #(.width(32)) register_3 (.D(PROGRAM_COUNTER), .en(1'b1), .clk(clk), .Q(PC_stored));  // open: clr
  control_logic control_logic_1 (
    .CSRWen(CSRWEn), .StoreSel(StoreSel), .LoadSel(LoadSel), .PCSel(PCSel), .RegWEn(RegWEn), .ImmSel(ImmSel),
    .BrUn(BrUn), .ASel(ASel), .BSel(BSel), .ALUSel(ALUSel), .MemRW(MemRW), .WBSel(WBSel), .CSRSel(CSRSel),
    .inst({CSR_address, register_1_q_2, register_1_q[14:12], register_1_q_3, register_1_q[6:0]}),
    .BrEq(BrEq), .BrLt(BrLt));
  regfile regfile_1 (
    .rs1(register_1_q_2), .rs2(CSR_address[4:0]), .rd(register_1_q_3), .Write_Data(WBData), .RegWEn(RegWEn),
    .clk(clk), .ra(ra), .sp(sp), .t0(t0), .t1(t1), .t2(t2), .s0(s0), .s1(s1), .a0(a0), .Read_Data_1(rs1),
    .Read_Data_2(rs2));
  imm_gen imm_gen_1 (
    .inst({CSR_address, register_1_q_2, register_1_q[14:12], register_1_q_3, register_1_q[6:0]}),
    .ImmSel(ImmSel), .imm(imm));
  Multiplexer #(.enable("false"), .width(32)) multiplexer_3 (
    .in0(PC_stored), .in1(rs1), .out(multiplexer_3_out), .sel(ASel));
  Multiplexer #(.enable("false"), .width(32)) multiplexer_4 (.in0(rs2), .in1(imm), .out(multiplexer_4_out), .sel(BSel));
  alu alu_1 (.Result(WRITE_ADDRESS), .A(multiplexer_3_out), .B(multiplexer_4_out), .ALUSel(ALUSel));
  branch_comp branch_comp_1 (.rs1(rs1), .rs2(rs2), .BrUn(BrUn), .BrEq(BrEq), .BrLt(BrLt));
  Multiplexer #(.enable("false"), .width(32)) multiplexer_5 (
    .in0(imm), .in1(rs1), .out(multiplexer_5_out), .sel(CSRSel));
  csr csr_1 (.CSR_address(CSR_address), .CSR_din(multiplexer_5_out), .CSR_WE(CSRWEn), .clk(clk), .tohost(tohost));
  Multiplexer #(.enable("false"), .select(2), .width(32)) multiplexer_6 (
    .in0({rs2[7:0], rs2[7:0], rs2[7:0], rs2[7:0]}), .in1({rs2[15:0], rs2[15:0]}), .in2(rs2),
    .out(WRITE_DATA), .sel(StoreSel));  // open: in3
  Multiplexer #(.enable("false"), .select(2), .width(32)) multiplexer_7 (
    .in0(PC_n_4), .in1(WRITE_ADDRESS), .in2(READ_DATA_FINAL), .out(WBData), .sel(WBSel));  // open: in3
  Multiplexer #(.enable("false"), .select(2), .width(4)) multiplexer_8 (
    .in0(4'b0001), .in1(4'b0010), .in2(4'b0100), .in3(4'b1000), .out(multiplexer_8_out),
    .sel(WRITE_ADDRESS[1:0]));
  Multiplexer #(.enable("false"), .select(2), .width(4)) multiplexer_9 (
    .in0(4'b0011), .in2(4'b1100), .out(multiplexer_9_out), .sel(WRITE_ADDRESS[1:0]));  // open: in1, in3
  Multiplexer #(.enable("false"), .select(2), .width(4)) multiplexer_10 (
    .in0(multiplexer_8_out), .in1(multiplexer_9_out), .in2(4'b1111), .out(multiplexer_10_out), .sel(StoreSel));  // open: in3
  Multiplexer #(.enable("false"), .width(4)) multiplexer_11 (
    .in0(4'b0000), .in1(multiplexer_10_out), .out(WRITE_ENABLE), .sel(MemRW));
  assign bit_extender_1_out = {{24{multiplexer_12_out[7]}}, multiplexer_12_out};  // Bit_Extender bit_extender_1
  Multiplexer #(.enable("false"), .select(2), .width(8)) multiplexer_12 (
    .in0(READ_DATA[7:0]), .in1(READ_DATA[15:8]), .in2(READ_DATA[23:16]), .in3(READ_DATA[31:24]),
    .out(multiplexer_12_out), .sel(WRITE_ADDRESS[1:0]));
  assign bit_extender_2_out = {{16{multiplexer_13_out[15]}}, multiplexer_13_out};  // Bit_Extender bit_extender_2
  Multiplexer #(.enable("false"), .select(2), .width(16)) multiplexer_13 (
    .in0(READ_DATA[15:0]), .in1(READ_DATA[23:8]), .in2(READ_DATA[31:16]), .out(multiplexer_13_out),
    .sel(WRITE_ADDRESS[1:0]));  // open: in3
  Multiplexer #(.enable("false"), .select(2), .width(32)) multiplexer_14 (
    .in0(bit_extender_1_out), .in1(bit_extender_2_out), .in2(READ_DATA), .out(READ_DATA_FINAL), .sel(LoadSel));  // open: in3

  // Other names for the same wires on the sheet: ALURes[31:0] = WRITE_ADDRESS; LSBs[1:0] = WRITE_ADDRESS[1:0]

  // Notes on the sheet:
  //   Output to IMEM
  //   IMEM (do **NOT** move this)
  //   Inputs from IMEM
  //   Inputs/Outputs for testing. Do **NOT** move these.
  //   Just a bunch of combinational logic
  //   PC
  //   rs1
  //   rs2
  //   imm
  //   Just a bunch of combinational logic
  //   imm
  //   rs1
  //   Outputs To DMEM
  //   DMEM (do **NOT** move this)
  //   Inputs From DMEM
endmodule
