// Logisim project imm_gen.circ as structural Verilog: 1 circuit, main circuit imm_gen
module imm_gen (
  input  [31:0] inst,
  input  [2:0] ImmSel,
  output [31:0] imm
);

  wire [31:0] bit_extender_1_out, bit_extender_2_out, bit_extender_3_out, bit_extender_4_out,
       bit_extender_5_out, bit_extender_6_out;

  assign bit_extender_1_out = {{20{inst[31]}}, inst[31:20]};  // Bit_Extender bit_extender_1
  assign bit_extender_2_out = {{20{inst[31]}}, {inst[31:25], inst[11:7]}};  // Bit_Extender bit_extender_2
  assign bit_extender_3_out = {{20{inst[31]}}, {inst[31], inst[7], inst[30:25], inst[11:8]}};  // Bit_Extender bit_extender_3
  assign bit_extender_4_out = {{12{inst[31]}}, inst[31:12]};  // Bit_Extender bit_extender_4
  assign bit_extender_5_out = {{12{inst[31]}}, {inst[31], inst[19:12], inst[20], inst[30:21]}};  // Bit_Extender bit_extender_5
  assign bit_extender_6_out = {{27{inst[19]}}, inst[19:15]};  // Bit_Extender bit_extender_6
  Multiplexer #(.enable("false"), .select(3), .width(32)) multiplexer_1 (
    .in0(bit_extender_1_out), .in1(bit_extender_2_out), .in2(bit_extender_3_out), .in3(bit_extender_4_out),
    .in4(bit_extender_5_out), .in5(bit_extender_6_out), .out(imm), .sel(ImmSel));  // open: in6, in7

  // Notes on the sheet:
  //   INPUTS to your circuit
  //   I-type
  //   S-type
  //   SB-type
  //   U-type
  //   UJ-type
  //   CSR
  //   DON'T CHANGE THE LOCATIONS OF THE INPUTS AND OUTPUTS!
  //   OUTPUT from your circuit
endmodule
