// Logisim project csr_test_harness.circ as structural Verilog: 1 circuit, main circuit test_harness
module test_harness (
  input  [31:0] INSTRUCTION,
  input  clk,
  output [31:0] PROGRAM_COUNTER,
  output [31:0] ra,
  output [31:0] sp,
  output [31:0] t0,
  output [31:0] t1,
  output [31:0] t2,
  output [31:0] s0,
  output [31:0] s1,
  output [31:0] a0,
  output [31:0] tohost
);

  wire [3:0] cpu_1_write_enable;
  wire [31:0] cpu_1_write_address, cpu_1_write_data, mem_1_p5;

  cpu cpu_1 (
    .clk(clk), .INSTRUCTION(INSTRUCTION), .READ_DATA(mem_1_p5), .WRITE_ADDRESS(cpu_1_write_address),
    .PROGRAM_COUNTER(PROGRAM_COUNTER), .ra(ra), .sp(sp), .t0(t0), .t1(t1), .t2(t2), .s0(s0), .s1(s1),
    .a0(a0), .tohost(tohost), .WRITE_ENABLE(cpu_1_write_enable), .WRITE_DATA(cpu_1_write_data));
  // mem mem_1: pin names not known; wires that end beside it: cpu_1_write_address, cpu_1_write_enable, cpu_1_write_data, clk, mem_1_p5

  // Notes on the sheet:
  //   YOUR CPU SHOULD FIT IN HERE!
endmodule
