// Logisim project cpu-selectionSort.circ as structural Verilog: 1 circuit, main circuit run_main
module run_main (
  output [31:0] ra,
  output [31:0] sp,
  output [31:0] t0,
  output [31:0] t1,
  output [31:0] t2,
  output [31:0] s0,
  output [31:0] s1,
  output [31:0] a0,
  output [31:0] Requested_Address,
  output [31:0] Requested_Instruction,
  output [15:0] Time_Step,
  output halt
);

  wire clk;

  Clock clock_1 (.out(clk));
  // Probe on Requested_Address
  // test_harness test_harness_1: pin names not known; wires that end beside it: Requested_Instruction, clk, Requested_Address, ra, sp, t0, t1, t2, s0, s1, a0
  ROM #(.addrWidth(14), .dataWidth(32)) rom_1 (.addr(Requested_Address[15:2]), .data(Requested_Instruction));
  // Probe on Requested_Instruction
  Counter #(.max('hffff), .width(16)) counter_1 (.clk(clk), .Q(Time_Step));  // open: clr, load, up, count, D, carry
  Comparator #(.width(16)) comparator_1 (.a(Time_Step), .b(16'h30b), .eq(halt));  // open: gt, lt

  // Other names for the same wires on the sheet: fetch_addr[31:0] = Requested_Address;
  //   Instruction[31:0] = Requested_Instruction

  // Notes on the sheet:
  //   contents of rom_1 (hex, n*v repeats v):
  //   00001537 00050513 00300293 00552023 00100293 00552223 00500293 00552423 00400293 00552623 00900293
  //   00552823 00000293 00552A23 00800293 00552C23 00600293 00552E23 00700293 02552023 00200293 02552223
  //   00A00593 060000EF 00001537 00050513 00052283 00452283 00852283 00C52283 01052283 01452283 01852283
  //   01C52283 02052283 02452283 00A00513 0F00006F 00259293 00550333 00032383 00261293 00550E33 000E2E83
  //   007E2023 01D32023 00008067 FD810113 00112023 00812223 00912423 01212623 01312823 01412A23 01512C23
  //   01612E23 03712023 03812223 00050413 00058493 FFF58913 00000993 00098293 05298C63 00299293 005402B3
  //   0002AB83 00098C13 00198B13 029B0463 002B1A13 01440AB3 000AA283 0172C463 00C0006F 00028B93 000B0C13
  //   001B0B13 FDDFF06F 00050513 00098593 000C0613 F51FF0EF 00198993 FA9FF06F 00012083 00412403 00812483
  //   00C12903 01012983 01412A03 01812A83 01C12B03 02012B83 02412C03 02810113 000080E7
  //   Instruction Memory
  //   Halts Execution After Constant # of Clock Cycles
  //   Constant
endmodule
